// Logisim project Processador.circ as structural Verilog
module registrador_4bit (
  input  clock,
  input  _3_pos_bit,
  input  _2_pos_bit,
  input  _1_pos_bit,
  input  _0_pos_bit,
  input  enable,
  output _3_pos_bit_2,
  output _2_pos_bit_2,
  output _1_pos_bit_2,
  output _0_pos_bit_2
);

  D_Flip_Flop d_ff_1 (.clk(clock), .D(_3_pos_bit), .Q(_3_pos_bit_2), .en(enable));  // open: Qn, preset, reset
  D_Flip_Flop d_ff_2 (.clk(clock), .D(_2_pos_bit), .Q(_2_pos_bit_2), .en(enable));  // open: Qn, preset, reset
  D_Flip_Flop d_ff_3 (.clk(clock), .D(_1_pos_bit), .Q(_1_pos_bit_2), .en(enable));  // open: Qn, preset, reset
  D_Flip_Flop d_ff_4 (.clk(clock), .D(_0_pos_bit), .Q(_0_pos_bit_2), .en(enable));  // open: Qn, preset, reset
endmodule

module registrador_8bit (
  input  clock,
  input  _7_pos_bit,
  input  _6_pos_bit,
  input  _5_pos_bit,
  input  _4_pos_bit,
  input  _3_pos_bit,
  input  _2_pos_bit,
  input  _1_pos_bit,
  input  _0_pos_bit,
  input  enable,
  output _7_pos_bit_2,
  output _6_pos_bit_2,
  output _5_pos_bit_2,
  output _4_pos_bit_2,
  output _3_pos_bit_2,
  output _2_pos_bit_2,
  output _1_pos_bit_2,
  output _0_pos_bit_2
);

  registrador_4bit registrador_4bit_1 (
    .clock(clock), ._3_pos_bit(_7_pos_bit), ._2_pos_bit(_6_pos_bit), ._1_pos_bit(_5_pos_bit),
    ._0_pos_bit(_4_pos_bit), ._3_pos_bit_2(_7_pos_bit_2), ._2_pos_bit_2(_6_pos_bit_2),
    ._1_pos_bit_2(_5_pos_bit_2), ._0_pos_bit_2(_4_pos_bit_2), .enable(enable));
  registrador_4bit registrador_4bit_2 (
    .clock(clock), ._3_pos_bit(_3_pos_bit), ._2_pos_bit(_2_pos_bit), ._1_pos_bit(_1_pos_bit),
    ._0_pos_bit(_0_pos_bit), ._3_pos_bit_2(_3_pos_bit_2), ._2_pos_bit_2(_2_pos_bit_2),
    ._1_pos_bit_2(_1_pos_bit_2), ._0_pos_bit_2(_0_pos_bit_2), .enable(enable));
endmodule

module Registrador_de_instrucao (
  input  clock,
  input  _11_pos_bit,
  input  _10_pos_bit,
  input  _9_pos_bit,
  input  _8_pos_bit,
  input  _7_pos_bit,
  input  _6_pos_bit,
  input  _5_pos_bit,
  input  _4_pos_bit,
  input  _3_pos_bit,
  input  _2_pos_bit,
  input  _1_pos_bit,
  input  _0_pos_bit,
  output op2,
  output op1,
  output op0,
  output rw_2,
  output rw_1,
  output rw_0,
  output R1_2,
  output R1_1,
  output R1_0,
  output X_2,
  output X_1,
  output X_0
);

  registrador_4bit registrador_4bit_1 (
    .clock(clock), ._3_pos_bit(_11_pos_bit), ._2_pos_bit(_10_pos_bit), ._1_pos_bit(_9_pos_bit),
    ._0_pos_bit(_8_pos_bit), ._3_pos_bit_2(op2), ._2_pos_bit_2(op1), ._1_pos_bit_2(op0), ._0_pos_bit_2(rw_2),
    .enable(1'b1));
  registrador_8bit registrador_8bit_1 (
    .clock(clock), ._7_pos_bit(_7_pos_bit), ._6_pos_bit(_6_pos_bit), ._5_pos_bit(_5_pos_bit),
    ._4_pos_bit(_4_pos_bit), ._3_pos_bit(_3_pos_bit), ._2_pos_bit(_2_pos_bit), ._1_pos_bit(_1_pos_bit),
    ._0_pos_bit(_0_pos_bit), ._7_pos_bit_2(rw_1), ._6_pos_bit_2(rw_0), ._5_pos_bit_2(R1_2),
    ._4_pos_bit_2(R1_1), ._3_pos_bit_2(R1_0), ._2_pos_bit_2(X_2), ._1_pos_bit_2(X_1), ._0_pos_bit_2(X_0),
    .enable(1'b1));
endmodule

module Banco_de_registradores (
  input  r1_2,
  input  r1_1,
  input  r1_0,
  input  Clock,
  input  wd_3,
  input  wd_2,
  input  wd_1,
  input  wd_0,
  input  rw_2,
  input  rw_1,
  input  rw_0,
  input  RegWrite,
  input  x_2,
  input  x_1,
  input  x_0,
  input  rImm,
  output r3,
  output r2,
  output r1,
  output r0,
  output x3,
  output x2,
  output x1,
  output x0
);

  wire _0_2_out_12, _1_2_out_12, _2_2_out_12, _3_2_out_12, R0__0_pos_bit_2, R0__1_pos_bit_2, R0__2_pos_bit_2,
       R0__3_pos_bit_2, R1__0_pos_bit_2, R1__1_pos_bit_2, R1__2_pos_bit_2, R1__3_pos_bit_2, R2__0_pos_bit_2,
       R2__1_pos_bit_2, R2__2_pos_bit_2, R2__3_pos_bit_2, R3__0_pos_bit_2, R3__1_pos_bit_2, R3__2_pos_bit_2,
       R3__3_pos_bit_2, R4__0_pos_bit_2, R4__1_pos_bit_2, R4__2_pos_bit_2, R4__3_pos_bit_2, R5__0_pos_bit_2,
       R5__1_pos_bit_2, R5__2_pos_bit_2, R5__3_pos_bit_2, R6__0_pos_bit_2, R6__1_pos_bit_2, R6__2_pos_bit_2,
       R6__3_pos_bit_2, R7__1_pos_bit_2, R7__2_pos_bit_2, R7__3_pos_bit_2;

  Demultiplexador_1_8 demultiplexador_1_8_1 (
    .control0(rw_0), .control1(rw_1), .control2(rw_2), .\input (RegWrite));  // open: _0, _1, _2, _3, _4, _5, _6, _7
  registrador_4bit u_R0 (
    .clock(Clock), ._3_pos_bit(wd_3), ._2_pos_bit(wd_2), ._1_pos_bit(wd_1), ._0_pos_bit(wd_0),
    ._3_pos_bit_2(R0__3_pos_bit_2), ._2_pos_bit_2(R0__2_pos_bit_2), ._1_pos_bit_2(R0__1_pos_bit_2),
    ._0_pos_bit_2(R0__0_pos_bit_2));  // open: enable
  registrador_4bit u_R1 (
    .clock(Clock), ._3_pos_bit(wd_3), ._2_pos_bit(wd_2), ._1_pos_bit(wd_1), ._0_pos_bit(wd_0),
    ._3_pos_bit_2(R1__3_pos_bit_2), ._2_pos_bit_2(R1__2_pos_bit_2), ._1_pos_bit_2(R1__1_pos_bit_2),
    ._0_pos_bit_2(R1__0_pos_bit_2));  // open: enable
  registrador_4bit u_R2 (
    .clock(Clock), ._3_pos_bit(wd_3), ._2_pos_bit(wd_2), ._1_pos_bit(wd_1), ._0_pos_bit(wd_0),
    ._3_pos_bit_2(R2__3_pos_bit_2), ._2_pos_bit_2(R2__2_pos_bit_2), ._1_pos_bit_2(R2__1_pos_bit_2),
    ._0_pos_bit_2(R2__0_pos_bit_2));  // open: enable
  registrador_4bit u_R3 (
    .clock(Clock), ._3_pos_bit(wd_3), ._2_pos_bit(wd_2), ._1_pos_bit(wd_1), ._0_pos_bit(wd_0),
    ._3_pos_bit_2(R3__3_pos_bit_2), ._2_pos_bit_2(R3__2_pos_bit_2), ._1_pos_bit_2(R3__1_pos_bit_2),
    ._0_pos_bit_2(R3__0_pos_bit_2), .enable(wd_3));
  Multiplexador_8_1 _3 (
    .control0(r1_0), .control1(r1_1), .control2(r1_2), .a(R0__3_pos_bit_2), .b(R1__3_pos_bit_2),
    .c(R2__3_pos_bit_2), .d(R3__3_pos_bit_2), .e(R4__3_pos_bit_2), .f(R5__3_pos_bit_2), .g(R6__3_pos_bit_2),
    .h(R7__3_pos_bit_2), .out_12(r3));
  Multiplexador_8_1 _3_2 (
    .control0(x_0), .control1(x_1), .control2(x_2), .a(R0__3_pos_bit_2), .b(R1__3_pos_bit_2),
    .c(R2__3_pos_bit_2), .d(R3__3_pos_bit_2), .e(R4__3_pos_bit_2), .f(R5__3_pos_bit_2), .g(R6__3_pos_bit_2),
    .h(R7__3_pos_bit_2), .out_12(_3_2_out_12));
  Multiplexador_2_1 multiplexador_2_1_1 (.control(rImm), .A(_3_2_out_12), .B(1'b0), .out_4(x3));
  Multiplexador_8_1 _2 (
    .control0(r1_0), .control1(r1_1), .control2(r1_2), .a(R0__2_pos_bit_2), .b(R1__2_pos_bit_2),
    .c(R2__2_pos_bit_2), .d(R3__2_pos_bit_2), .e(R4__2_pos_bit_2), .f(R5__2_pos_bit_2), .g(R6__2_pos_bit_2),
    .h(R7__2_pos_bit_2), .out_12(r2));
  Multiplexador_8_1 _2_2 (
    .control0(x_0), .control1(x_1), .control2(x_2), .a(R0__2_pos_bit_2), .b(R1__2_pos_bit_2),
    .c(R2__2_pos_bit_2), .d(R3__2_pos_bit_2), .e(R4__2_pos_bit_2), .f(R5__2_pos_bit_2), .g(R6__2_pos_bit_2),
    .h(R7__2_pos_bit_2), .out_12(_2_2_out_12));
  Multiplexador_2_1 multiplexador_2_1_2 (.control(rImm), .A(_2_2_out_12), .B(x_2), .out_4(x2));
  Multiplexador_8_1 _1 (
    .control0(r1_0), .control1(r1_1), .control2(r1_2), .a(R0__1_pos_bit_2), .b(R1__1_pos_bit_2),
    .c(R2__1_pos_bit_2), .d(R3__1_pos_bit_2), .e(R4__1_pos_bit_2), .f(R5__1_pos_bit_2), .g(R6__1_pos_bit_2),
    .h(R7__1_pos_bit_2), .out_12(r1));
  Multiplexador_8_1 _1_2 (
    .control0(x_0), .control1(x_1), .control2(x_2), .a(R0__1_pos_bit_2), .b(R1__1_pos_bit_2),
    .c(R2__1_pos_bit_2), .d(R3__1_pos_bit_2), .e(R4__1_pos_bit_2), .f(R5__1_pos_bit_2), .g(R6__1_pos_bit_2),
    .h(R7__1_pos_bit_2), .out_12(_1_2_out_12));
  Multiplexador_2_1 multiplexador_2_1_3 (.control(rImm), .A(_1_2_out_12), .B(x_1), .out_4(x1));
  Multiplexador_8_1 _0 (
    .control0(r1_0), .control1(r1_1), .control2(r1_2), .a(R0__0_pos_bit_2), .b(R1__0_pos_bit_2),
    .c(R2__0_pos_bit_2), .d(R3__0_pos_bit_2), .e(R4__0_pos_bit_2), .f(R5__0_pos_bit_2), .g(R6__0_pos_bit_2),
    .h(wd_3), .out_12(r0));
  Multiplexador_8_1 _0_2 (
    .control0(x_0), .control1(x_1), .control2(x_2), .a(R0__0_pos_bit_2), .b(R1__0_pos_bit_2),
    .c(R2__0_pos_bit_2), .d(R3__0_pos_bit_2), .e(R4__0_pos_bit_2), .f(R5__0_pos_bit_2), .g(R6__0_pos_bit_2),
    .h(wd_3), .out_12(_0_2_out_12));
  Multiplexador_2_1 multiplexador_2_1_4 (.control(rImm), .A(_0_2_out_12), .B(x_0), .out_4(x0));
  registrador_4bit R4 (
    .clock(Clock), ._3_pos_bit(wd_3), ._2_pos_bit(wd_2), ._1_pos_bit(wd_1), ._0_pos_bit(wd_0),
    ._3_pos_bit_2(R4__3_pos_bit_2), ._2_pos_bit_2(R4__2_pos_bit_2), ._1_pos_bit_2(R4__1_pos_bit_2),
    ._0_pos_bit_2(R4__0_pos_bit_2));  // open: enable
  registrador_4bit R5 (
    .clock(Clock), ._3_pos_bit(wd_3), ._2_pos_bit(wd_2), ._1_pos_bit(wd_1), ._0_pos_bit(wd_0),
    ._3_pos_bit_2(R5__3_pos_bit_2), ._2_pos_bit_2(R5__2_pos_bit_2), ._1_pos_bit_2(R5__1_pos_bit_2),
    ._0_pos_bit_2(R5__0_pos_bit_2));  // open: enable
  registrador_4bit R6 (
    .clock(Clock), ._3_pos_bit(wd_3), ._2_pos_bit(wd_2), ._1_pos_bit(wd_1), ._0_pos_bit(wd_0),
    ._3_pos_bit_2(R6__3_pos_bit_2), ._2_pos_bit_2(R6__2_pos_bit_2), ._1_pos_bit_2(R6__1_pos_bit_2),
    ._0_pos_bit_2(R6__0_pos_bit_2));  // open: enable
  registrador_4bit R7 (
    .clock(Clock), ._3_pos_bit(wd_3), ._2_pos_bit(wd_2), ._1_pos_bit(wd_1), ._0_pos_bit(wd_0),
    ._3_pos_bit_2(R7__3_pos_bit_2), ._2_pos_bit_2(R7__2_pos_bit_2), ._1_pos_bit_2(R7__1_pos_bit_2),
    ._0_pos_bit_2(wd_3));  // open: enable

  // Notes on the sheet:
  //   rw deve escolhber para onde mandar o clock e passar o wd
  //   r1 = register 1 source
  //   rw = register to write to
  //   x = register or immediate source
  //   wd = write data from the ALU
endmodule

module Multiplexador_2_1 (
  input  control,
  input  A,
  input  B,
  output out_4
);

  wire and_1_out, and_2_out, not_1_out;

  not not_1 (not_1_out, control);
  and and_1 (and_1_out, not_1_out, A);
  or or_1 (out_4, and_1_out, and_2_out);
  and and_2 (and_2_out, B, control);
endmodule

module Multiplexador_4_1 (
  input  control0,
  input  control1,
  input  a,
  input  b,
  input  c,
  input  d,
  output out_7
);

  wire multiplexador_2_1_1_out_4, multiplexador_2_1_2_out_4;

  Multiplexador_2_1 multiplexador_2_1_1 (.control(control0), .A(a), .B(b), .out_4(multiplexador_2_1_1_out_4));
  Multiplexador_2_1 multiplexador_2_1_2 (.control(control0), .A(c), .B(d), .out_4(multiplexador_2_1_2_out_4));
  Multiplexador_2_1 multiplexador_2_1_3 (
    .control(control1), .A(multiplexador_2_1_1_out_4), .B(multiplexador_2_1_2_out_4), .out_4(out_7));
endmodule

module Multiplexador_8_1 (
  input  control0,
  input  control1,
  input  control2,
  input  a,
  input  b,
  input  c,
  input  d,
  input  e,
  input  f,
  input  g,
  input  h,
  output out_12
);

  wire multiplexador_4_1_1_out_7, multiplexador_4_1_2_out_7;

  Multiplexador_4_1 multiplexador_4_1_1 (
    .control0(control0), .control1(control1), .a(a), .b(b), .c(c), .d(d), .out_7(multiplexador_4_1_1_out_7));
  Multiplexador_2_1 multiplexador_2_1_1 (
    .control(control2), .A(multiplexador_4_1_1_out_7), .B(multiplexador_4_1_2_out_7), .out_4(out_12));
  Multiplexador_4_1 multiplexador_4_1_2 (
    .control0(control0), .control1(control1), .a(e), .b(f), .c(g), .d(h), .out_7(multiplexador_4_1_2_out_7));
endmodule

module adder (
  input  A,
  input  B,
  input  CarryIn,
  output carryOut,
  output Sum
);

  wire and_1_out, and_2_out, xor_1_out;

  or or_1 (carryOut, and_1_out, and_2_out);
  and and_1 (and_1_out, A, B);
  and and_2 (and_2_out, CarryIn, xor_1_out);
  xor xor_1 (xor_1_out, A, B);
  xor xor_2 (Sum, CarryIn, xor_1_out);

  // Notes on the sheet:
  //   carry das entradas
  //   carry do carry in
endmodule

module add_sub (
  input  a3,
  input  b3,
  input  a2,
  input  b2,
  input  a1,
  input  b1,
  input  a0,
  input  b0,
  input  Sub,
  output CarryOut,
  output s3,
  output s2,
  output s1,
  output s0
);

  wire adder_2_carryout, adder_3_carryout, adder_4_carryout, xor_1_out, xor_2_out, xor_3_out, xor_4_out;

  xor xor_1 (xor_1_out, b3, Sub);
  adder adder_1 (.carryOut(CarryOut), .A(a3), .B(xor_1_out), .Sum(s3), .CarryIn(adder_2_carryout));
  adder adder_2 (.carryOut(adder_2_carryout), .A(a2), .B(xor_2_out), .Sum(s2), .CarryIn(adder_3_carryout));
  xor xor_2 (xor_2_out, b2, Sub);
  xor xor_3 (xor_3_out, b1, Sub);
  adder adder_3 (.carryOut(adder_3_carryout), .A(a1), .B(xor_3_out), .Sum(s1), .CarryIn(adder_4_carryout));
  xor xor_4 (xor_4_out, b0, Sub);
  adder adder_4 (.carryOut(adder_4_carryout), .A(a0), .B(xor_4_out), .Sum(s0), .CarryIn(Sub));
endmodule

module Demultiplexador_1_2 (
  input  control,
  input  \input ,
  output out_3,
  output out_4
);

  wire not_1_out;

  not not_1 (not_1_out, control);
  and and_1 (out_3, not_1_out, \input );
  and and_2 (out_4, control, \input );
endmodule

module Demultiplexador_1_8 (
  input  control0,
  input  control1,
  input  control2,
  input  \input ,
  output _0,
  output _1,
  output _2,
  output _3,
  output _4,
  output _5,
  output _6,
  output _7
);

  wire demultiplexador_1_2_1_out_3, demultiplexador_1_2_1_out_4, demultiplexador_1_2_2_out_3,
       demultiplexador_1_2_2_out_4, demultiplexador_1_2_3_out_3, demultiplexador_1_2_3_out_4;

  Demultiplexador_1_2 demultiplexador_1_2_1 (
    .control(control2), .\input (\input ), .out_3(demultiplexador_1_2_1_out_3),
    .out_4(demultiplexador_1_2_1_out_4));
  Demultiplexador_1_2 demultiplexador_1_2_2 (
    .control(control1), .\input (demultiplexador_1_2_1_out_3), .out_3(demultiplexador_1_2_2_out_3),
    .out_4(demultiplexador_1_2_2_out_4));
  Demultiplexador_1_2 demultiplexador_1_2_3 (
    .control(control1), .\input (demultiplexador_1_2_1_out_4), .out_3(demultiplexador_1_2_3_out_3),
    .out_4(demultiplexador_1_2_3_out_4));
  Demultiplexador_1_2 demultiplexador_1_2_4 (
    .control(control0), .\input (demultiplexador_1_2_2_out_3), .out_3(_0), .out_4(_1));
  Demultiplexador_1_2 demultiplexador_1_2_5 (
    .control(control0), .\input (demultiplexador_1_2_2_out_4), .out_3(_2), .out_4(_3));
  Demultiplexador_1_2 demultiplexador_1_2_6 (
    .control(control0), .\input (demultiplexador_1_2_3_out_3), .out_3(_4), .out_4(_5));
  Demultiplexador_1_2 demultiplexador_1_2_7 (
    .control(control0), .\input (demultiplexador_1_2_3_out_4), .out_3(_6), .out_4(_7));
endmodule
